# Fritzing sketch locked-in-light-schematic (saved by Fritzing 1.0.3b)
breadboards: 1

parts:
  S1 = Round Pushbutton
  Mod1 = ESP32-TTGO-T-DISPLAY
  HC-SR04_Sensor_1 = HC-SR04 Ultrasonic Distance Sensor

nets:
  N1: S1.leg0, Mod1.G-1, Mod1.G-2, Mod1.G-10, Mod1.G-11, Mod1.G-14, HC-SR04_Sensor_1.GND
  N2: S1.leg1, Mod1.37
  N3: Mod1.3V, HC-SR04_Sensor_1.VCC
  N4: Mod1.27, HC-SR04_Sensor_1.ECHO
  N5: Mod1.26, HC-SR04_Sensor_1.TRIG

custom parts:
  ESP32-TTGO-T-DISPLAY: LILYGO TTGO T-Display GD32VF103CBT6 Main Chip ST7789 1.14 Inch IPS 240x135 Resolution Minimalist Development Board.
